// Logisim project lab3.circ as structural Verilog: 1 circuit, main circuit main
module main (
  input  [31:0] Instruction
);

  wire alu_control_1_alusrc, clock_1_out;
  wire [3:0] alu_control_1_aluctrl0;
  wire [31:0] alu32_1_r, bit_extender_1_out, multiplexer_1_out, register_file_1_rdata1,
       register_file_1_rdata2;

  Clock clock_1 (.out(clock_1_out));
  assign bit_extender_1_out = {{20{Instruction[31]}}, Instruction[31:20]};  // Bit_Extender bit_extender_1
  register_file register_file_1 (
    .RReg2(Instruction[19:15]), .RReg1(Instruction[24:20]), .WData(alu32_1_r), .Clock_in(clock_1_out),
    .Write(1'b1), .WReg(Instruction[11:7]), .RData1(register_file_1_rdata1), .RData2(register_file_1_rdata2));
  ALU_Control alu_control_1 (
    .I30(Instruction[30]), .I14(Instruction[14]), .I13(Instruction[13]), .I12(Instruction[12]),
    .I6(Instruction[6]), .I5(Instruction[5]), .I4(Instruction[4]), .ALUCTRL3(alu_control_1_aluctrl0[3]),
    .ALUCTRL2(alu_control_1_aluctrl0[2]), .ALUCTRL1(alu_control_1_aluctrl0[1]),
    .ALUCTRL0(alu_control_1_aluctrl0[0]), .ALUSRC(alu_control_1_alusrc));
  Multiplexer #(.enable("false"), .width(32)) multiplexer_1 (
    .in0(register_file_1_rdata2), .in1(bit_extender_1_out), .out(multiplexer_1_out),
    .sel(alu_control_1_alusrc));
  ALU32 alu32_1 (
    .ALU_Ctrl(alu_control_1_aluctrl0), .A(register_file_1_rdata1), .B(multiplexer_1_out), .R(alu32_1_r));  // open: C_out
endmodule
